// Digital circuit reg4.dig as structural Verilog
module reg4 (
  input  Write,
  input  e_3,
  input  e_2,
  input  e_1,
  input  e_0,
  output s_3,
  output s_2,
  output s_1,
  output s_0
);

  D_FF d_ff_1 (.D(e_3), .C(Write), .Q(s_3));  // open: nQ
  D_FF d_ff_2 (.D(e_2), .C(Write), .Q(s_2));  // open: nQ
  D_FF d_ff_3 (.D(e_1), .C(Write), .Q(s_1));  // open: nQ
  D_FF d_ff_4 (.D(e_0), .C(Write), .Q(s_0));  // open: nQ
endmodule
