// Digital circuit reg4_e_s.dig as structural Verilog
module reg4_e_s (
  input  Write,
  input  Read,
  input  e_3,
  input  e_2,
  input  e_1,
  input  e_0,
  output s_3,
  output s_2,
  output s_1,
  output s_0
);

  wire d_ff_1_q, d_ff_2_q, d_ff_3_q, d_ff_4_q;

  D_FF d_ff_1 (.D(e_3), .C(Write), .Q(d_ff_1_q));  // open: nQ
  assign s_3 = Read ? d_ff_1_q : 1'bz;  // Driver driver_1
  D_FF d_ff_2 (.D(e_2), .C(Write), .Q(d_ff_2_q));  // open: nQ
  assign s_2 = Read ? d_ff_2_q : 1'bz;  // Driver driver_2
  D_FF d_ff_3 (.D(e_1), .C(Write), .Q(d_ff_3_q));  // open: nQ
  assign s_1 = Read ? d_ff_3_q : 1'bz;  // Driver driver_3
  D_FF d_ff_4 (.D(e_0), .C(Write), .Q(d_ff_4_q));  // open: nQ
  assign s_0 = Read ? d_ff_4_q : 1'bz;  // Driver driver_4
endmodule
