// Digital circuit Eje2-boolean-function.dig as structural Verilog
module Eje2_boolean_function (
  input  E2,
  input  E1,
  input  E0,
  output S
);

  wire nor_1_out, not_1_out, or_1_out;

  or or_1 (or_1_out, E2, E1, E0);
  nor nor_1 (nor_1_out, E2, E1);
  not not_1 (not_1_out, nor_1_out);
  and and_1 (S, not_1_out, or_1_out);
endmodule

/* Test case:
E2	E1	E0	S
0	0	0	0
0	0	1	0
0	1	0	1
0	1	1	1
1	0	0	1
1	0	1	1
1	1	0	1
1	1	1	1
*/
